# Fritzing sketch 4digit8segment (saved by Fritzing 0.9.3b)
breadboards: 1

parts:
  Parça1 = Arduino Uno (Rev3)
  R1 = Resistor [tolerance=±5% resistance=1k package="2512 [SMD]"]
  U2 = 7-SEGMENT-4DIGIT-YOUNGSUN [package=7-segment-4digit-youngsun-longpads]
  Q1 = TRANSISTOR_NPN [package=to-92-ammo]
  Q2 = TRANSISTOR_NPN [package=to-92-ammo]
  Q3 = TRANSISTOR_NPN [package=to-92-ammo]
  R4 = Resistor [tolerance=±5% resistance=1k package="2512 [SMD]"]
  R5 = Resistor [tolerance=±5% resistance=1k package="2512 [SMD]"]
  R7 = Resistor [tolerance=±5% resistance=220 package=THT]
  R8 = Resistor [tolerance=±5% resistance=220 package=THT]
  R10 = Resistor [tolerance=±5% resistance=220 package=THT]
  R11 = Resistor [tolerance=±5% resistance=220 package=THT]
  R13 = Resistor [tolerance=±5% resistance=220 package=THT]
  R14 = Resistor [tolerance=±5% resistance=220 package=THT]
  R15 = Resistor [tolerance=±5% resistance=220 package=THT]
  S1 = Pushbutton [package="[THT]"]  # not connected
  S2 = Pushbutton [package="[THT]"]  # not connected
  R16 = Resistor [tolerance=±5% resistance=10k package=THT]
  R17 = Resistor [tolerance=±5% resistance=10k package=THT]

nets:
  N1: Parça1.A0, R17.Pin_0
  N2: Parça1.A1, R16.Pin_0
  N3: Parça1.D11_PWM/MOSI, R8.Pin_0
  N4: Parça1.D12/MISO, R15.Pin_1
  N5: Parça1.D3_PWM, R5.Pin_1
  N6: Parça1.D4, R4.Pin_1
  N7: Parça1.D5_PWM, R1.Pin_1
  N8: Parça1.D6_PWM, R7.Pin_0
  N9: Parça1.D7, R10.Pin_0
  N10: Parça1.GND, Q1.E, Q2.E, Q3.E, R16.Pin_1, R17.Pin_1
  N11: R1.Pin_0, Q3.B
  N12: U2.DIG1, R13.Pin_0
  N13: U2.DIG2, R14.Pin_0
  N14: U2.COL-A, R11.Pin_0
  N15: U2.E, R15.Pin_0
  N16: U2.DIG3, Q3.C
  N17: U2.F, R10.Pin_1
  N18: U2.COL-C, Q1.C
  N19: U2.C, Q2.C
  N20: U2.A, R8.Pin_1
  N21: U2.G, R7.Pin_1
  N22: Q1.B, R4.Pin_0
  N23: Q2.B, R5.Pin_0
